// Logisim project FULLadder.circ as structural Verilog: 1 circuit, main circuit main
module main (
  input  A,
  input  B,
  input  Cin,
  output SUM,
  output CARRY_OUT
);

  wire AND_2_out, AND_3_out, AND_out, XOR_out;

  xor XOR (XOR_out, A, B);
  and AND (AND_out, A, B);
  and AND_2 (AND_2_out, B, Cin);
  and AND_3 (AND_3_out, Cin, A);
  xor XOR_2 (SUM, XOR_out, Cin);
  or OR (CARRY_OUT, AND_out, AND_2_out, AND_3_out);

  // Notes on the sheet:
  //   (S)
  //   (C out)
endmodule
