// Logisim project HALFadder.circ as structural Verilog: 1 circuit, main circuit main
module main (
  input  A,
  input  B,
  output SUM__S,
  output CARRY__C
);

  xor XOR (SUM__S, A, B);
  and AND_CARRY (CARRY__C, A, B);
endmodule
