// Logisim project hall and full adder project.circ as structural Verilog: 1 circuit, main circuit main
module main (
  input  in_1,
  input  [3:0] in_2,
  input  in_3,
  input  [3:0] in_4,
  input  in_5,
  input  in_6,
  input  in_7,
  input  in_8,
  input  in_9,
  input  in_10,
  input  [3:0] in_11,
  input  [4:0] in_12,
  input  [3:0] in_13,
  input  in_14,
  input  in_15,
  input  in_16,
  input  in_17,
  input  in_18,
  input  in_19,
  output SUM,
  output out_21,
  output out_22,
  output out_23
);

  wire and_2_out, and_3_out, and_4_out, xor_2_out;
  wire [3:0] adder_1_out, adder_2_out;
  wire [4:0] bit_extender_1_out, bit_extender_2_out;

  xor xor_1 (SUM, in_3, in_6);
  and and_1 (out_22, in_8, in_10);
  DotMatrix #(.inputtype("row"), .matrixcols(4), .matrixrows(1), .dotshape("circle")) dotmatrix_1 (.row0({in_19, in_18, in_17, in_16}));
  xor xor_2 (xor_2_out, in_1, in_5);
  and and_2 (and_2_out, in_9, in_9, in_14, in_14);
  and and_3 (and_3_out, in_14, in_15);
  and and_4 (and_4_out, in_9, in_15);
  xor xor_3 (out_21, xor_2_out, in_7);
  or or_1 (out_23, and_2_out, and_3_out, and_4_out);
  Adder #(.width(4)) adder_1 (.a(in_2), .b(in_4), .out(adder_1_out));  // open: cin, cout
  assign bit_extender_1_out = {{1{1'b0}}, adder_2_out};  // Bit_Extender bit_extender_1
  Adder #(.width(4)) adder_2 (.a(in_11), .b(in_13), .out(adder_2_out));  // open: cin, cout
  DotMatrix #(.inputtype("row"), .matrixrows(1), .dotshape("circle")) dotmatrix_2 (.row0(bit_extender_2_out));
  assign bit_extender_2_out = {{1{1'b0}}, adder_1_out};  // Bit_Extender bit_extender_2

  // Notes on the sheet:
  //   HALF ADDER
  //   CARRY
  //   FULL ADDER
  //   ADDER VIA 4-BIT EXTENDER WITH HELP OF LED MATRIX 
  //   ADDER VIA 4-BIT EXTENDER WITH HELP OF 5 BIT OUTPUT
endmodule
